# Fritzing sketch circuit design (saved by Fritzing 0.9.3b)
breadboards: 1

parts:
  U1 = XIAO ESP32C3
  Mod1 = AD8232 HeartRate Monitor [part_number=SEN-12650]
  Btn1 = Adafruit Push-button Power Switch Breakout [package=THT]
  Grove1 = Grove OLED 128x96
  Lipo_battery = LIPO-110mAh [package=lipo-110]  # not connected
  NEOPIXEL1 = Neopixel Strip -- White (30/m)
  Power_plug1 = USB-C plug  # not connected

nets:
  N1: U1.D0, Mod1.OUTPUT
  N2: U1.D4, Grove1.SDA
  N3: U1.D5, Grove1.SCL
  N4: U1.D6, Btn1.OUT
  N5: U1.D10, NEOPIXEL1.Din
  3V3: U1.3V3, Mod1.3.3v, Btn1.IN, Grove1.VCC, NEOPIXEL1.+5V
  GND: U1.GND, Mod1.GND, Mod1.LO-, Mod1.LO+, Btn1.GND, Grove1.GND, NEOPIXEL1.GND

notes:
  LiPo battery is connected to USB-C power input on the reverse side (not shown in breadboard layout)

custom parts:
  XIAO ESP32C3: Seeed Studio XIAO ESP32C3 adopts new RISC-V architecture, supporting both Wi-Fi and BLE wireless connectivities. For Internet of Things applications, you will find it is flexible and suitable for all kinds of IoT scenarios.
  AD8232 HeartRate Monitor: Sparkfun single lead heart rate monitor - Ad8232.
  Neopixel Strip -- White (30/m): These NeoPixel strips have 30 digitally-addressable pixel LEDs per meter and are very affordable and are only 12.5 mm wide, 10 mm if you remove the strip from the casing.
  USB-C plug: power plug
